// Digital circuit Decoder.dig as structural Verilog
module Decoder (
  input  [31:0] Instruction,
  output [15:0] A,
  output [15:0] B
);


  assign A = Instruction[15:0];
  assign B = Instruction[31:16];
endmodule
