// Digital circuit CPU.dig as structural Verilog
module CPU (
  input  [15:0] A,
  input  [15:0] B,
  output [15:0] O
);

  wire [15:0] decoder_1_a, decoder_1_b;

  Decoder decoder_1 (.Instruction({B, A}), .A(decoder_1_a), .B(decoder_1_b));
  Execute execute_1 (.A(decoder_1_a), .B(decoder_1_b), .Result(O));
endmodule
