// Digital circuit CPU.dig as structural Verilog
module CPU (
  input  [15:0] A,
  input  [7:0] B,
  input  [15:0] A_2,
  input  [7:0] B_3,
  input  [15:0] A_3,
  input  [7:0] B_4,
  input  [15:0] A_4,
  input  [7:0] B_5,
  output [15:0] B_2,
  output [15:0] R0,
  output [15:0] R1,
  output [15:0] R2,
  output [15:0] R3
);

  wire button_1_out;
  wire [1:0] decoder_1_rd, decoder_1_rs, PC_out;
  wire [15:0] decoder_1_a, execute_1_result;
  wire [31:0] multiplexer_1_out;

  Multiplexer #(.Selector_Bits(2), .Bits(32)) multiplexer_1 (
    .sel(PC_out), .in_0({{8{1'b0}}, B, A}), .in_1({{8{1'b0}}, B_3, A_2}), .in_2({{8{1'b0}}, B_4, A_3}),
    .in_3({{8{1'b0}}, B_5, A_4}), .out(multiplexer_1_out));
  Counter #(.Bits(2)) PC (.en(1'b1), .C(button_1_out), .clr(1'b0), .out(PC_out));  // open: ovf
  Button button_1 (.out(button_1_out));
  Decoder decoder_1 (.Instruction(multiplexer_1_out), .A(decoder_1_a), .rs(decoder_1_rs), .rd(decoder_1_rd));
  Execute execute_1 (.A(decoder_1_a), .B(B_2), .Result(execute_1_result));
  Register_File register_file_1 (
    .rs(decoder_1_rs), .rd(decoder_1_rd), .Result(execute_1_result), .Clock(button_1_out), .B(B_2), .R0(R0),
    .R1(R1), .R2(R2), .R3(R3));

  // Notes on the sheet:
  //   A: default 100
  //   B: default 1
  //   A_2: default 200
  //   B_3: default 18
  //   A_3: default 99
  //   B_4: default 35
  //   A_4: default 34
  //   B_5: default 48
endmodule
