// Digital circuit Execute.dig as structural Verilog
module Execute (
  input  [15:0] A,
  input  [15:0] B,
  output [15:0] Result
);

  Add #(.Bits(16)) add_1 (.a(A), .b(B), .c_i(1'b0), .s(Result));  // open: c_o
endmodule
