// Digital circuit CPU.dig as structural Verilog
module CPU (
  input  [15:0] imm,
  input  [1:0] dest,
  input  [1:0] src,
  output [15:0] B,
  output [15:0] R0,
  output [15:0] R1,
  output [15:0] R2,
  output [15:0] R3,
  output [1:0] rd,
  output [1:0] rs,
  output [15:0] A,
  output [3:0] PC,
  output [15:0] A_2
);

  wire Add, add_out, assembler_1_store_clk, button_1_out, Jump, jump_out, Mode_out;
  wire [15:0] execute_1_result;
  wire [31:0] assembler_1_inst, Program_d;

  LED Programming (.in(Mode_out));
  DipSwitch Mode (.out(Mode_out));
  Button u_add (.out(add_out));
  Button u_jump (.out(jump_out));
  Assembler assembler_1 (
    .Mode(Mode_out), .imm(imm), .dest(dest), .src(src), .add(add_out), .jump(jump_out),
    .inst(assembler_1_inst), .store_clk(assembler_1_store_clk));
  Button button_1 (.out(button_1_out));
  CounterPreset #(.Bits(4), .isProgramCounter("true")) u_PC (
    .en(1'b1), .C(button_1_out), .dir(1'b0), .in(A[3:0]), .ld(Jump), .clr(1'b0), .out(PC));  // open: ovf
  EEPROMDualPort #(.AddrBits(4), .Bits(32)) Program (
    .A(PC), .Din(assembler_1_inst), .str(1'b1), .C(assembler_1_store_clk), .ld(1'b1), .D(Program_d));
  LED led_1 (.in(Jump));
  LED led_2 (.in(Add));
  Decoder decoder_1 (
    .Prog(Mode_out), .Bypass(assembler_1_inst), .Instruction(Program_d), .A(A), .rs(rs), .rd(rd), .add(Add),
    .jump(Jump));
  Execute execute_1 (.A(A), .B(B), .Add(Add), .Result(execute_1_result));
  Register_File register_file_1 (
    .rs(rs), .rd(rd), .Result(execute_1_result), .Clock(button_1_out), .B(B), .R0(R0), .R1(R1), .R2(R2),
    .R3(R3));

  assign A_2 = A;

  // Notes on the sheet:
  //   contents of Program (hex, n*v repeats v):
  //   64,100c8,120063,230022,30002a,7000001
  //   PC =
  //   R
  //   =
  //   +
  //   (
  //   )
endmodule
