// Digital circuit Execute.dig as structural Verilog
module Execute (
  input  [15:0] A,
  input  [15:0] B,
  input  Add,
  output [15:0] Result
);

  wire [15:0] add_1_s;

  Add #(.Bits(16)) add_1 (.a(A), .b(B), .c_i(1'b0), .s(add_1_s));  // open: c_o
  Multiplexer #(.Bits(16)) multiplexer_1 (.sel(Add), .in_0(B), .in_1(add_1_s), .out(Result));
endmodule
